# Fritzing sketch fritziing_ChristmasLights (saved by Fritzing 0.9.3b)

parts:
  Arduino1 = Arduino Nano (Rev3.0)
  S1 = Pushbutton [package="[THT]"]
  NEOPIXEL1 = Neopixel Strip -- White (30/m)

nets:
  GND: Arduino1.GND, S1.Pin_3, S1.Pin_4, NEOPIXEL1.GND
  N1: Arduino1.D4, NEOPIXEL1.Din
  N2: Arduino1.D5, S1.Pin_1, S1.Pin_2
  VIN: Arduino1.VIN, NEOPIXEL1.+5V

custom parts:
  Neopixel Strip -- White (30/m): These NeoPixel strips have 30 digitally-addressable pixel LEDs per meter and are very affordable and are only 12.5 mm wide, 10 mm if you remove the strip from the casing.
